# Fritzing sketch Gross (saved by Fritzing 1.0.3b)
stripboards: 1

parts:
  Part1 = SparkFun LiPo Fuel Gauge [part_number=TOL-20680]
  A3 = LX-LCBST
  S1 = 0.91 inch OLED I2C Display 128 x 32 Pixels
  Q1 = Basic FET N-Channel [package="DPak [SMD]"]
  Sensor1 = TTP223B Capacitive Touch Sensor Module
  Sensor2 = TTP223B Capacitive Touch Sensor Module
  R1 = Resistor [tolerance=±5% power=0.25W resistance=10k package=THT]
  A5 = Esp32-c3 super mini
  Load_Cell1 = Load Cell - Red/white/black/green
  Load_Cell2 = Load Cell - Red/white/black/green
  U1 = LIPO-1000mAh [package=lipo-1000]  # not connected
  A6 = Sparkfun load cell amplifier
  A7 = Sparkfun load cell amplifier
  R2 = Resistor [tolerance=±5% power=0.25W resistance=220 package=THT]

nets:
  N1: Part1.SDA, A5.Pin_4
  N2: Part1.SCL, A5.Pin_5
  N3: Part1.V_BATT, A3.Pin_2
  N4: Part1.GND, A3.Pin_1
  N5: A3.Pin_3, Q1.source, R1.Pin_1, A5.Pin_15
  VCC: A3.Pin_4, S1.VCC, Sensor1.VCC, Sensor2.VCC, A5.Pin_16, A6.Pin_10, A7.Pin_10
  GND: S1.GND, Q1.drain, Sensor1.GND, A6.Pin_6, A7.Pin_6
  N6: S1.SDA, A5.Pin_13
  N7: S1.SCL, A5.Pin_12
  N8: Q1.Gate, R1.Pin_0, R2.Pin_0
  N9: Sensor1.SIG, A5.Pin_10
  N10: Sensor2.SIG, A5.Pin_9
  N11: A5.Pin_1, R2.Pin_1
  N12: A5.Pin_3, A6.Pin_7, A7.Pin_7
  N13: A5.Pin_7, A7.Pin_8
  N14: A5.Pin_8, A6.Pin_8
  N15: Load_Cell1.wire1, A7.Pin_1
  N16: Load_Cell1.wire2, A7.Pin_3
  N17: Load_Cell1.wire3, A7.Pin_2
  N18: Load_Cell1.wire4, A7.Pin_4
  N19: Load_Cell2.wire1, A6.Pin_1
  N20: Load_Cell2.wire2, A6.Pin_3
  N21: Load_Cell2.wire3, A6.Pin_2
  N22: Load_Cell2.wire4, A6.Pin_4

custom parts:
  SparkFun LiPo Fuel Gauge: LiPo batteries are a great way to power your projects. They're small, lightweight, and pack a good punch for their size. Unfortunately, even the best batteries eventually run low on power, and when they do it's often unexpected (and at the worst time). Don't be caught by surprise next time your board suddenly powers down! The SparkFun LiPo Fuel Gauge connects your battery to your project and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
  LX-LCBST: Lithium Li-ion 18650 3.7V 4.2V Battery Charger Board DC-DC Step Up Boost Module TP4056 DIY Kit Parts.
  TTP223B Capacitive Touch Sensor Module: The TTP223B capacitive touch sensor module uses the TTP223B IC. The appropriate voltage is approximately 2 to 5.5 volts.
  Esp32-c3 super mini: ESP32-C3 Development Board ESP32 SuperMini Development Board ESP32 Development Board WiFi Bluetooth.
  Load Cell - Red/white/black/green: A rectangle load cell/weighting pressure Sensor with four wires - Red, white, black, green. Normally corresponding with E+, E-, A+, A- respectively.
  Sparkfun load cell amplifier: The SparkFun Load Cell Amplifier is a small breakout board for the HX711 IC that allows you to easily read load cells to measure weight.
